// Logisim project 2H.circ as structural Verilog: 1 circuit, main circuit main
module main (
  input  in_1,
  input  in_2,
  input  in_3,
  input  in_4,
  output out_5,
  output out_6,
  output out_7,
  output out_8,
  output out_9,
  output out_10,
  output out_11,
  output out_12,
  output out_13,
  output out_14,
  output out_15,
  output out_16,
  output out_17,
  output out_18,
  output out_19,
  output out_20
);

  wire not_1_out, not_3_out, not_4_out;

  not not_1 (not_1_out, in_1);
  not not_2 (not_1_out, in_2);
  not not_3 (not_3_out, in_3);
  not not_4 (not_4_out, in_4);
  and and_1 (out_5, not_4_out, not_3_out, not_1_out, not_1_out);
  and and_2 (out_6, in_4, not_3_out, not_1_out, not_1_out);
  and and_3 (out_7, in_4, in_3, not_1_out, not_1_out);
  and and_4 (out_8, in_4, in_3, not_1_out, not_1_out);
  and and_5 (out_9, not_4_out, not_3_out, in_2, not_1_out);
  and and_6 (out_10, in_4, not_3_out, in_2, not_1_out);
  and and_7 (out_11, not_4_out, in_2, not_1_out);
  and and_8 (out_12, in_4, in_3, in_2, not_1_out);
  and and_9 (out_13, not_4_out, not_3_out, not_1_out, in_1);
  and and_10 (out_14, in_4, not_3_out, not_1_out, in_1);
  and and_11 (out_15, not_4_out, in_3, not_1_out, in_1);
  and and_12 (out_16, not_3_out, in_3, not_1_out, in_1);
  and and_13 (out_17, not_4_out, not_3_out, in_2, in_1);
  and and_14 (out_18, in_4, not_3_out, in_2, in_1);
  and and_15 (out_19, not_4_out, in_3, in_2, in_1);
  and and_16 (out_20, in_4, in_3, in_2, in_1);
endmodule
