// Logisim project 4H.circ as structural Verilog: 1 circuit, main circuit main
module main (
  input  in_1,
  input  in_2,
  input  in_3,
  input  in_4,
  input  in_5,
  input  in_6,
  input  in_7,
  input  in_8,
  input  in_9,
  input  in_10,
  input  in_11,
  input  in_12,
  input  in_13,
  input  in_14,
  input  in_15,
  input  in_16,
  input  in_17,
  output out_18,
  output out_19,
  output out_20,
  output out_21,
  output out_22,
  output out_23,
  output out_24,
  output out_25,
  output out_26
);

  wire main_1_c0, main_2_c0, main_3_c0, main_4_c0, main_5_c0, main_6_c0, main_7_c0;

  full_adder_main main_1 (.A(in_2), .B(in_3), .Ci(in_1), .C0(main_1_c0), .S(out_18));
  full_adder_main main_2 (.A(in_4), .B(in_5), .Ci(main_1_c0), .C0(main_2_c0), .S(out_19));
  full_adder_main main_3 (.A(in_6), .B(in_7), .Ci(main_2_c0), .C0(main_3_c0), .S(out_20));
  full_adder_main main_4 (.A(in_8), .B(in_9), .Ci(main_3_c0), .C0(main_4_c0), .S(out_21));
  full_adder_main main_5 (.A(in_10), .B(in_11), .Ci(main_4_c0), .C0(main_5_c0), .S(out_22));
  full_adder_main main_6 (.A(in_12), .B(in_13), .Ci(main_5_c0), .C0(main_6_c0), .S(out_23));
  full_adder_main main_7 (.A(in_14), .B(in_15), .Ci(main_6_c0), .C0(main_7_c0), .S(out_24));
  full_adder_main main_8 (.A(in_16), .B(in_17), .Ci(main_7_c0), .C0(out_26), .S(out_25));
endmodule
