// Logisim project easy-tasks.circ as structural Verilog: 1 circuit, main circuit main
module main (
  input  in_1,
  input  in_2,
  input  in_3,
  input  in_4,
  input  in_5,
  input  in_6,
  input  in_7,
  input  in_8,
  input  in_9,
  input  in_10,
  input  in_11,
  input  in_12,
  input  in_13,
  input  in_14,
  input  in_15,
  input  in_16,
  input  in_17,
  input  in_18,
  input  in_19,
  input  in_20,
  input  in_21,
  input  in_22,
  input  in_23,
  input  in_24,
  input  in_25,
  input  in_26,
  output out_27,
  output out_28,
  output out_29,
  output out_30,
  output out_31,
  output out_32,
  output out_33,
  output out_34,
  output out_35
);

  wire and_1_out, nand_1_out, nand_3_out, nand_4_out, nand_6_out, nand_7_out, nor_1_out, nor_2_out,
       nor_3_out, nor_5_out, nor_7_out, or_1_out, or_2_out, or_4_out, or_5_out, or_6_out, xor_1_out;

  nand nand_1 (nand_1_out, in_1, in_3);
  nor nor_1 (nor_1_out, in_5, in_7);
  and and_1 (and_1_out, in_9, in_11);
  or or_1 (or_1_out, in_16, in_18);
  or or_2 (or_2_out, in_20, in_22);
  nand nand_2 (out_35, in_25, in_25);
  nand nand_3 (nand_3_out, in_1, nand_1_out);
  nand nand_4 (nand_4_out, nand_1_out, in_3);
  nor nor_2 (nor_2_out, in_5, nor_1_out);
  nor nor_3 (nor_3_out, nor_1_out, in_7);
  and and_2 (out_31, and_1_out, in_13);
  or or_3 (out_33, or_1_out, or_2_out);
  nand nand_5 (out_27, nand_3_out, nand_4_out);
  nor nor_4 (out_29, nor_2_out, nor_3_out);
  nand nand_6 (nand_6_out, in_12, in_14);
  nand nand_7 (nand_7_out, in_15, in_17);
  or or_4 (or_4_out, in_19, in_21);
  or or_5 (or_5_out, in_24, in_26);
  nor nor_5 (nor_5_out, in_2, in_2);
  nor nor_6 (out_28, nor_5_out, nor_7_out);
  nor nor_7 (nor_7_out, in_4, in_4);
  xor xor_1 (xor_1_out, in_6, in_8);
  nor nor_8 (out_32, nand_6_out, nand_7_out);
  or or_6 (or_6_out, or_4_out, in_23);
  or or_7 (out_34, or_6_out, or_5_out);
  xor xor_2 (out_30, xor_1_out, in_10);
endmodule
