// Logisim project full-adder.circ as structural Verilog: 1 circuit, main circuit main
module main (
  input  Ci,
  input  A,
  input  B,
  output S,
  output C0
);

  wire and_1_out, and_2_out, xor_1_out;

  xor xor_1 (xor_1_out, A, B);
  and and_1 (and_1_out, A, B);
  xor xor_2 (S, xor_1_out, Ci);
  and and_2 (and_2_out, xor_1_out, Ci);
  or or_1 (C0, and_2_out, and_1_out);
endmodule
